// Logisim project arch1lab_progetto.circ as structural Verilog: 9 circuits, main circuit main
module main (
);

  wire button_2_out, button_3_out, button_out, clock_1_out, priority_encoder_1_gs, Reset_out, v_out;
  wire [1:0] i00, i01, i02, i03, i04, i05, i06, i07, i08, i09, i10, i11, i12, i13, i14, i15,
       priority_encoder_1_out, register_1_q, y00, y01, y02, y03, y04, y05, y06, y07, y08, y09, y10, y11, y12,
       y13, y14, y15;
  wire [3:0] c00, c01, c02, c03, c04, c05, c06, c07, c08, c09, c10, c11, c12, c13, c14, c15,
       cell_1_state_south, cell_2_state_north, cell_2_state_south, cell_3_state_north, cell_3_state_south,
       cell_4_state_north, cell_5_state_south, cell_5_state_west, cell_6_state_north, cell_6_state_south,
       cell_6_state_west, cell_7_state_north, cell_7_state_south, cell_7_state_west, cell_8_state_north,
       cell_8_state_west, cell_9_state_south, cell_9_state_west, cell_10_state_north, cell_10_state_south,
       cell_10_state_west, cell_11_state_north, cell_11_state_south, cell_11_state_west, cell_12_state_north,
       cell_12_state_west, cell_13_state_south, cell_13_state_west, cell_14_state_north, cell_14_state_south,
       cell_14_state_west, cell_15_state_north, cell_15_state_south, cell_15_state_west, cell_16_state_north,
       cell_16_state_west;

  Button button (.out(button_out));
  Button button_2 (.out(button_2_out));
  Button v (.out(v_out));
  Hex_Digit_Display hex_digit_display_1 (.value(c00));  // open: dp
  Hex_Digit_Display hex_digit_display_2 (.value(c04));  // open: dp
  Hex_Digit_Display hex_digit_display_3 (.value(c08));  // open: dp
  Hex_Digit_Display hex_digit_display_4 (.value(c12));  // open: dp
  Button button_3 (.out(button_3_out));
  Hex_Digit_Display hex_digit_display_5 (.value(c01));  // open: dp
  Hex_Digit_Display hex_digit_display_6 (.value(c05));  // open: dp
  Hex_Digit_Display hex_digit_display_7 (.value(c09));  // open: dp
  Hex_Digit_Display hex_digit_display_8 (.value(c13));  // open: dp
  Hex_Digit_Display hex_digit_display_9 (.value(c02));  // open: dp
  Hex_Digit_Display hex_digit_display_10 (.value(c06));  // open: dp
  Hex_Digit_Display hex_digit_display_11 (.value(c10));  // open: dp
  Hex_Digit_Display hex_digit_display_12 (.value(c14));  // open: dp
  Priority_Encoder #(.select(2)) priority_encoder_1 (
    .in0(button_3_out), .in1(button_2_out), .in2(button_out), .in3(v_out), .out(priority_encoder_1_out),
    .gs(priority_encoder_1_gs));  // open: en_out, en_in
  Hex_Digit_Display hex_digit_display_13 (.value(c03));  // open: dp
  Hex_Digit_Display hex_digit_display_14 (.value(c07));  // open: dp
  Hex_Digit_Display hex_digit_display_15 (.value(c11));  // open: dp
  Hex_Digit_Display hex_digit_display_16 (.value(c15));  // open: dp
  Register #(.width(2)) register_1 (
    .D(priority_encoder_1_out), .Q(register_1_q), .clk(priority_encoder_1_gs));  // open: en, clr
  Button Reset (.out(Reset_out));
  uc uc_1 (
    .in_3(y00), .in_4(y01), .in_5(y02), .in_6(y03), .in_7(y04), .in_8(y05), .in_9(y06), .in_10(y07),
    .in_11(y08), .in_12(y09), .in_13(y10), .in_14(y11), .in_15(y12), .in_16(y13), .in_17(y14), .in_18(y15),
    .in_1(priority_encoder_1_gs), .in_2(register_1_q), .in_19(Reset_out), .in_20(clock_1_out), .out_21(i00),
    .out_22(i01), .out_23(i02), .out_24(i03), .out_25(i04), .out_26(i05), .out_27(i06), .out_28(i07),
    .out_29(i08), .out_30(i09), .out_31(i10), .out_32(i11), .out_33(i12), .out_34(i13), .out_35(i14),
    .out_36(i15));
  Clock clock_1 (.out(clock_1_out));
  \cell  cell_1 (
    .In_West(4'b0000), .State_East(c00), .In_East(cell_5_state_west), .In_North(4'b0000), .Cell_In(i00),
    .Direction(register_1_q), .In_South(cell_2_state_north), .Cell_Out(y00),
    .State_South(cell_1_state_south), .Clock(clock_1_out));  // open: State_West, State_North
  \cell  cell_2 (
    .In_West(4'b0000), .State_East(c04), .In_East(cell_6_state_west), .In_North(cell_1_state_south),
    .Cell_In(i04), .State_North(cell_2_state_north), .Direction(register_1_q), .In_South(cell_3_state_north),
    .Cell_Out(y04), .State_South(cell_2_state_south), .Clock(clock_1_out));  // open: State_West
  \cell  cell_3 (
    .In_West(4'b0000), .State_East(c08), .In_East(cell_7_state_west), .In_North(cell_2_state_south),
    .Cell_In(i08), .State_North(cell_3_state_north), .Direction(register_1_q), .In_South(cell_4_state_north),
    .Cell_Out(y08), .State_South(cell_3_state_south), .Clock(clock_1_out));  // open: State_West
  \cell  cell_4 (
    .In_West(4'b0000), .State_East(c12), .In_East(cell_8_state_west), .In_North(cell_3_state_south),
    .Cell_In(i12), .State_North(cell_4_state_north), .Direction(register_1_q), .In_South(4'b0000),
    .Cell_Out(y12), .Clock(clock_1_out));  // open: State_West, State_South
  \cell  cell_5 (
    .State_West(cell_5_state_west), .In_West(c00), .State_East(c01), .In_East(cell_9_state_west),
    .In_North(4'b0000), .Cell_In(i01), .Direction(register_1_q), .In_South(cell_6_state_north),
    .Cell_Out(y01), .State_South(cell_5_state_south), .Clock(clock_1_out));  // open: State_North
  \cell  cell_6 (
    .State_West(cell_6_state_west), .In_West(c04), .State_East(c05), .In_East(cell_10_state_west),
    .In_North(cell_5_state_south), .Cell_In(i05), .State_North(cell_6_state_north), .Direction(register_1_q),
    .In_South(cell_7_state_north), .Cell_Out(y05), .State_South(cell_6_state_south), .Clock(clock_1_out));
  \cell  cell_7 (
    .State_West(cell_7_state_west), .In_West(c08), .State_East(c09), .In_East(cell_11_state_west),
    .In_North(cell_6_state_south), .Cell_In(i09), .State_North(cell_7_state_north), .Direction(register_1_q),
    .In_South(cell_8_state_north), .Cell_Out(y09), .State_South(cell_7_state_south), .Clock(clock_1_out));
  \cell  cell_8 (
    .State_West(cell_8_state_west), .In_West(c12), .State_East(c13), .In_East(cell_12_state_west),
    .In_North(cell_7_state_south), .Cell_In(i13), .State_North(cell_8_state_north), .Direction(register_1_q),
    .In_South(4'b0000), .Cell_Out(y13), .Clock(clock_1_out));  // open: State_South
  \cell  cell_9 (
    .State_West(cell_9_state_west), .In_West(c01), .State_East(c02), .In_East(cell_13_state_west),
    .In_North(4'b0000), .Cell_In(i02), .Direction(register_1_q), .In_South(cell_10_state_north),
    .Cell_Out(y02), .State_South(cell_9_state_south), .Clock(clock_1_out));  // open: State_North
  \cell  cell_10 (
    .State_West(cell_10_state_west), .In_West(c05), .State_East(c06), .In_East(cell_14_state_west),
    .In_North(cell_9_state_south), .Cell_In(i06), .State_North(cell_10_state_north),
    .Direction(register_1_q), .In_South(cell_11_state_north), .Cell_Out(y06),
    .State_South(cell_10_state_south), .Clock(clock_1_out));
  \cell  cell_11 (
    .State_West(cell_11_state_west), .In_West(c09), .State_East(c10), .In_East(cell_15_state_west),
    .In_North(cell_10_state_south), .Cell_In(i10), .State_North(cell_11_state_north),
    .Direction(register_1_q), .In_South(cell_12_state_north), .Cell_Out(y10),
    .State_South(cell_11_state_south), .Clock(clock_1_out));
  \cell  cell_12 (
    .State_West(cell_12_state_west), .In_West(c13), .State_East(c14), .In_East(cell_16_state_west),
    .In_North(cell_11_state_south), .Cell_In(i14), .State_North(cell_12_state_north),
    .Direction(register_1_q), .In_South(4'b0000), .Cell_Out(y14), .Clock(clock_1_out));  // open: State_South
  \cell  cell_13 (
    .State_West(cell_13_state_west), .In_West(c02), .State_East(c03), .In_East(4'b0000), .In_North(4'b0000),
    .Cell_In(i03), .Direction(register_1_q), .In_South(cell_14_state_north), .Cell_Out(y03),
    .State_South(cell_13_state_south), .Clock(clock_1_out));  // open: State_North
  \cell  cell_14 (
    .State_West(cell_14_state_west), .In_West(c06), .State_East(c07), .In_East(4'b0000),
    .In_North(cell_13_state_south), .Cell_In(i07), .State_North(cell_14_state_north),
    .Direction(register_1_q), .In_South(cell_15_state_north), .Cell_Out(y07),
    .State_South(cell_14_state_south), .Clock(clock_1_out));
  \cell  cell_15 (
    .State_West(cell_15_state_west), .In_West(c10), .State_East(c11), .In_East(4'b0000),
    .In_North(cell_14_state_south), .Cell_In(i11), .State_North(cell_15_state_north),
    .Direction(register_1_q), .In_South(cell_16_state_north), .Cell_Out(y11),
    .State_South(cell_15_state_south), .Clock(clock_1_out));
  \cell  cell_16 (
    .State_West(cell_16_state_west), .In_West(c14), .State_East(c15), .In_East(4'b0000),
    .In_North(cell_15_state_south), .Cell_In(i15), .State_North(cell_16_state_north),
    .Direction(register_1_q), .In_South(4'b0000), .Cell_Out(y15), .Clock(clock_1_out));  // open: State_South
endmodule

// Compare
module compare (
  input  [3:0] In,
  input  [3:0] State,
  output NonZero,
  output Equal
);

  wire nor_1_out, xor_1_out, xor_2_out, xor_3_out, xor_4_out;

  xor xor_1 (xor_1_out, In[0], State[0]);
  xor xor_2 (xor_2_out, In[1], State[1]);
  xor xor_3 (xor_3_out, In[2], State[2]);
  xor xor_4 (xor_4_out, In[3], State[3]);
  or or_1 (NonZero, State[0], State[1], State[2], State[3]);
  nor nor_1 (nor_1_out, xor_1_out, xor_2_out, xor_3_out, xor_4_out);
  and and_1 (Equal, nor_1_out, NonZero);
endmodule

// NextState
module next_state (
  input  PlayLock,
  input  [7:0] State_Row,
  output [1:0] NextState_Cell3,
  output [1:0] NextState_Cell2,
  output [1:0] NextState_Cell1,
  output [1:0] NextState_Cell0,
  output Stable
);

  wire and_2_out, and_3_out, and_4_out, and_5_out, and_6_out, not_1_out, not_2_out, not_3_out, not_4_out,
       or_1_out, or_2_out, or_3_out, or_4_out;

  and and_1 (Stable, ~State_Row[7], ~State_Row[5], ~State_Row[3], ~State_Row[1], or_1_out);  // AND_Gate
  not not_1 (not_1_out, State_Row[6]);
  and and_2 (and_2_out, State_Row[5], ~State_Row[3], ~State_Row[1], State_Row[2], State_Row[0]);  // AND_Gate
  not not_2 (not_2_out, State_Row[4]);
  and and_3 (and_3_out, State_Row[3], ~State_Row[1], State_Row[0]);  // AND_Gate
  not not_3 (not_3_out, State_Row[2]);
  not not_4 (not_4_out, State_Row[0]);
  and and_4 (and_4_out, State_Row[0], State_Row[2], State_Row[4]);
  and and_5 (and_5_out, State_Row[0], ~State_Row[4], ~State_Row[6]);  // AND_Gate
  and and_6 (and_6_out, ~State_Row[2], ~State_Row[4], ~State_Row[6]);  // AND_Gate
  or or_1 (or_1_out, and_6_out, and_5_out, and_4_out);
  or or_2 (or_2_out, not_1_out, and_2_out, or_3_out);
  or or_3 (or_3_out, not_2_out, and_3_out, or_4_out);
  or or_4 (or_4_out, not_3_out, State_Row[1], not_4_out);
  and and_7 (NextState_Cell3[0], PlayLock, or_2_out);
  and and_8 (NextState_Cell2[1], and_2_out, PlayLock);
  and and_9 (NextState_Cell2[0], PlayLock, or_3_out);
  and and_10 (NextState_Cell1[1], and_3_out, PlayLock);
  and and_11 (NextState_Cell1[0], PlayLock, or_4_out);
  and and_12 (NextState_Cell0[1], State_Row[1], PlayLock);
  and and_13 (NextState_Cell0[0], PlayLock, not_4_out);

  assign NextState_Cell3[1] = State_Row[7];
endmodule

module \cell  (
  input  [3:0] In_North,
  input  [1:0] Cell_In,
  input  [1:0] Direction,
  input  [3:0] In_West,
  input  [3:0] In_East,
  input  [3:0] In_South,
  input  Clock,
  output [3:0] State_North,
  output [3:0] State_East,
  output [3:0] State_West,
  output [3:0] State_South,
  output [1:0] Cell_Out
);

  wire and_1_out;
  wire [3:0] adder_1_out, multiplexer_1_out, multiplexer_2_out;

  Multiplexer #(.select(2), .width(4)) multiplexer_1 (
    .in0(In_West), .in1(In_East), .in2(In_South), .in3(In_North), .out(multiplexer_1_out), .sel(Direction));  // open: en
  Adder #(.width(4)) adder_1 (.a(State_East), .b(4'b0000), .out(adder_1_out), .cin(Cell_In[1]));  // open: cout
  compare compare_1 (.In(multiplexer_1_out), .State(State_East), .NonZero(Cell_Out[0]), .Equal(Cell_Out[1]));
  Multiplexer #(.width(4)) multiplexer_2 (
    .in0(adder_1_out), .in1(multiplexer_1_out), .out(multiplexer_2_out), .sel(Cell_In[0]));  // open: en
  Register #(.width(4)) register_1 (.D(multiplexer_2_out), .Q(State_East), .clk(Clock), .clr(and_1_out));  // open: en
  and and_1 (and_1_out, Cell_In[1], Cell_In[0], ~Clock);  // AND_Gate

  assign State_North = State_East;
  assign State_South = State_East;
  assign State_West = State_East;
endmodule

module uc (
  input  in_1,
  input  [1:0] in_2,
  input  [1:0] in_3,
  input  [1:0] in_4,
  input  [1:0] in_5,
  input  [1:0] in_6,
  input  [1:0] in_7,
  input  [1:0] in_8,
  input  [1:0] in_9,
  input  [1:0] in_10,
  input  [1:0] in_11,
  input  [1:0] in_12,
  input  [1:0] in_13,
  input  [1:0] in_14,
  input  [1:0] in_15,
  input  [1:0] in_16,
  input  [1:0] in_17,
  input  [1:0] in_18,
  input  in_19,
  input  in_20,
  output [1:0] out_21,
  output [1:0] out_22,
  output [1:0] out_23,
  output [1:0] out_24,
  output [1:0] out_25,
  output [1:0] out_26,
  output [1:0] out_27,
  output [1:0] out_28,
  output [1:0] out_29,
  output [1:0] out_30,
  output [1:0] out_31,
  output [1:0] out_32,
  output [1:0] out_33,
  output [1:0] out_34,
  output [1:0] out_35,
  output [1:0] out_36
);

  wire fsm_1_playout, fsm_1_plus_1, or_1_out, play_1_out_35, random_1_out_18, random_1_out_19,
       random_1_out_20, random_1_out_21, random_1_out_22, random_1_out_23, random_1_out_24, random_1_out_25,
       random_1_out_26, random_1_out_27, random_1_out_28, random_1_out_29, random_1_out_30, random_1_out_31,
       random_1_out_32, random_1_out_33;
  wire [1:0] or_11_out, play_1_y00, play_1_y01, play_1_y02, play_1_y03, play_1_y04, play_1_y05, play_1_y06,
       play_1_y07, play_1_y08, play_1_y09, play_1_y10, play_1_y11, play_1_y12, play_1_y13, play_1_y14,
       play_1_y15;
  wire [1:1] or_2_out, or_3_out, or_4_out, or_5_out, or_6_out, or_7_out, or_8_out, or_9_out, or_10_out,
       or_12_out, or_13_out, or_14_out, or_15_out, or_16_out, or_17_out;
  wire [3:0] fsm_1_randomnum;

  fsm fsm_1 (
    .PlayOut(fsm_1_playout), .plus_1(fsm_1_plus_1), .ResetOut(or_11_out[0]), .RandomNum(fsm_1_randomnum),
    .Unstable(play_1_out_35), .PlayIn(in_1), .ResetIn(in_19), .Clock(in_20));
  random random_1 (
    .in_1(fsm_1_randomnum), .in_2(in_3[0]), .in_3(in_4[0]), .in_4(in_5[0]), .in_5(in_6[0]), .in_6(in_7[0]),
    .in_7(in_8[0]), .in_8(in_9[0]), .in_9(in_10[0]), .in_10(in_11[0]), .in_11(in_12[0]), .in_12(in_13[0]),
    .in_13(in_14[0]), .in_14(in_15[0]), .in_15(in_16[0]), .in_16(in_17[0]), .in_17(in_18[0]),
    .out_18(random_1_out_18), .out_19(random_1_out_19), .out_20(random_1_out_20), .out_21(random_1_out_21),
    .out_22(random_1_out_22), .out_23(random_1_out_23), .out_24(random_1_out_24), .out_25(random_1_out_25),
    .out_26(random_1_out_26), .out_27(random_1_out_27), .out_28(random_1_out_28), .out_29(random_1_out_29),
    .out_30(random_1_out_30), .out_31(random_1_out_31), .out_32(random_1_out_32), .out_33(random_1_out_33));
  play play_1 (
    .in_1(fsm_1_playout), .in_3(in_3), .in_4(in_4), .in_5(in_5), .in_6(in_6), .in_7(in_7), .in_8(in_8),
    .in_9(in_9), .in_10(in_10), .in_11(in_11), .in_12(in_12), .in_13(in_13), .in_14(in_14), .in_15(in_15),
    .in_16(in_16), .in_17(in_17), .in_18(in_18), .in_2(in_2), .y00(play_1_y00), .y01(play_1_y01),
    .y02(play_1_y02), .y03(play_1_y03), .y04(play_1_y04), .y05(play_1_y05), .y06(play_1_y06),
    .y07(play_1_y07), .y08(play_1_y08), .y09(play_1_y09), .y10(play_1_y10), .y11(play_1_y11),
    .y12(play_1_y12), .y13(play_1_y13), .y14(play_1_y14), .y15(play_1_y15), .out_35(play_1_out_35));
  or or_1 (or_1_out, fsm_1_plus_1, or_11_out[0]);
  or or_2 (or_2_out[1], or_11_out[0], random_1_out_18);
  or or_3 (or_3_out[1], or_11_out[0], random_1_out_19);
  or or_4 (or_4_out[1], or_11_out[0], random_1_out_20);
  or or_5 (or_5_out[1], or_11_out[0], random_1_out_21);
  or or_6 (or_6_out[1], or_11_out[0], random_1_out_22);
  or or_7 (or_7_out[1], or_11_out[0], random_1_out_23);
  or or_8 (or_8_out[1], or_11_out[0], random_1_out_24);
  or or_9 (or_9_out[1], or_11_out[0], random_1_out_25);
  or or_10 (or_10_out[1], or_11_out[0], random_1_out_26);
  or or_11 (or_11_out[1], or_11_out[0], random_1_out_27);
  or or_12 (or_12_out[1], or_11_out[0], random_1_out_28);
  or or_13 (or_13_out[1], or_11_out[0], random_1_out_29);
  or or_14 (or_14_out[1], or_11_out[0], random_1_out_30);
  or or_15 (or_15_out[1], or_11_out[0], random_1_out_31);
  or or_16 (or_16_out[1], or_11_out[0], random_1_out_32);
  or or_17 (or_17_out[1], or_11_out[0], random_1_out_33);
  Multiplexer #(.width(2)) multiplexer_1 (
    .in0(play_1_y00), .in1({or_2_out[1], or_11_out[0]}), .out(out_21), .sel(or_1_out));  // open: en
  Multiplexer #(.width(2)) multiplexer_2 (
    .in0(play_1_y01), .in1({or_3_out[1], or_11_out[0]}), .out(out_22), .sel(or_1_out));  // open: en
  Multiplexer #(.width(2)) multiplexer_3 (
    .in0(play_1_y02), .in1({or_4_out[1], or_11_out[0]}), .out(out_23), .sel(or_1_out));  // open: en
  Multiplexer #(.width(2)) multiplexer_4 (
    .in0(play_1_y03), .in1({or_5_out[1], or_11_out[0]}), .out(out_24), .sel(or_1_out));  // open: en
  Multiplexer #(.width(2)) multiplexer_5 (
    .in0(play_1_y04), .in1({or_6_out[1], or_11_out[0]}), .out(out_25), .sel(or_1_out));  // open: en
  Multiplexer #(.width(2)) multiplexer_6 (
    .in0(play_1_y05), .in1({or_7_out[1], or_11_out[0]}), .out(out_26), .sel(or_1_out));  // open: en
  Multiplexer #(.width(2)) multiplexer_7 (
    .in0(play_1_y06), .in1({or_8_out[1], or_11_out[0]}), .out(out_27), .sel(or_1_out));  // open: en
  Multiplexer #(.width(2)) multiplexer_8 (
    .in0(play_1_y07), .in1({or_9_out[1], or_11_out[0]}), .out(out_28), .sel(or_1_out));  // open: en
  Multiplexer #(.width(2)) multiplexer_9 (
    .in0(play_1_y08), .in1({or_10_out[1], or_11_out[0]}), .out(out_29), .sel(or_1_out));  // open: en
  Multiplexer #(.width(2)) multiplexer_10 (
    .in0(play_1_y09), .in1(or_11_out), .out(out_30), .sel(or_1_out));  // open: en
  Multiplexer #(.width(2)) multiplexer_11 (
    .in0(play_1_y10), .in1({or_12_out[1], or_11_out[0]}), .out(out_31), .sel(or_1_out));  // open: en
  Multiplexer #(.width(2)) multiplexer_12 (
    .in0(play_1_y11), .in1({or_13_out[1], or_11_out[0]}), .out(out_32), .sel(or_1_out));  // open: en
  Multiplexer #(.width(2)) multiplexer_13 (
    .in0(play_1_y12), .in1({or_14_out[1], or_11_out[0]}), .out(out_33), .sel(or_1_out));  // open: en
  Multiplexer #(.width(2)) multiplexer_14 (
    .in0(play_1_y13), .in1({or_15_out[1], or_11_out[0]}), .out(out_34), .sel(or_1_out));  // open: en
  Multiplexer #(.width(2)) multiplexer_15 (
    .in0(play_1_y14), .in1({or_16_out[1], or_11_out[0]}), .out(out_35), .sel(or_1_out));  // open: en
  Multiplexer #(.width(2)) multiplexer_16 (
    .in0(play_1_y15), .in1({or_17_out[1], or_11_out[0]}), .out(out_36), .sel(or_1_out));  // open: en
endmodule

module fsm (
  input  PlayIn,
  input  ResetIn,
  input  Unstable,
  input  Clock,
  output PlayOut,
  output plus_1,
  output ResetOut,
  output [3:0] RandomNum
);

  wire and_1_out, and_2_out, and_3_out, and_4_out, and_5_out, and_6_out, and_7_out, or_1_out, or_2_out,
       or_3_out, Q0_q, Q1_q, Q2_q;

  and and_1 (and_1_out, PlayIn, ~Q1_q, ~Q2_q);  // AND_Gate
  and and_2 (and_2_out, PlayIn, ~Q2_q, Q0_q);  // AND_Gate
  and and_3 (and_3_out, PlayIn, Unstable, ~Q2_q);  // AND_Gate
  and and_4 (and_4_out, Unstable, ~Q2_q, Q0_q);  // AND_Gate
  and and_5 (and_5_out, Q1_q, Q0_q);
  and and_6 (and_6_out, ~PlayIn, Q0_q);  // AND_Gate
  and and_7 (and_7_out, Q2_q, Q1_q, Q0_q);
  or or_1 (or_1_out, and_1_out, and_2_out, and_3_out, and_4_out, ResetIn);
  or or_2 (or_2_out, Q2_q, and_5_out, and_6_out, ResetIn);
  or or_3 (or_3_out, and_7_out, ResetIn);
  Random #(.width(4)) random_1 (.clk(Clock), .out(RandomNum));  // open: next, clr
  D_Flip_Flop Q0 (.clk(Clock), .D(or_1_out), .Q(Q0_q));  // open: Qn, preset, en, reset
  D_Flip_Flop Q1 (.clk(Clock), .D(or_2_out), .Q(Q1_q));  // open: Qn, preset, en, reset
  D_Flip_Flop Q2 (.clk(Clock), .D(or_3_out), .Q(Q2_q));  // open: Qn, preset, en, reset
  and and_8 (PlayOut, Q0_q, Q1_q, ~Q2_q);  // AND_Gate
  and and_9 (plus_1, ~Q0_q, Q1_q);  // AND_Gate
  and and_10 (ResetOut, Q0_q, Q1_q, Q2_q);
endmodule

module play (
  input  in_1,
  input  [1:0] in_2,
  input  [1:0] in_3,
  input  [1:0] in_4,
  input  [1:0] in_5,
  input  [1:0] in_6,
  input  [1:0] in_7,
  input  [1:0] in_8,
  input  [1:0] in_9,
  input  [1:0] in_10,
  input  [1:0] in_11,
  input  [1:0] in_12,
  input  [1:0] in_13,
  input  [1:0] in_14,
  input  [1:0] in_15,
  input  [1:0] in_16,
  input  [1:0] in_17,
  input  [1:0] in_18,
  output [1:0] y00,
  output [1:0] y01,
  output [1:0] y02,
  output [1:0] y03,
  output [1:0] y04,
  output [1:0] y05,
  output [1:0] y06,
  output [1:0] y07,
  output [1:0] y08,
  output [1:0] y09,
  output [1:0] y10,
  output [1:0] y11,
  output [1:0] y12,
  output [1:0] y13,
  output [1:0] y14,
  output [1:0] y15,
  output out_35
);

  wire next_state_1_stable, next_state_2_stable, next_state_3_stable, next_state_4_stable;
  wire [1:0] next_state_1_nextstate_cell0, next_state_1_nextstate_cell1, next_state_1_nextstate_cell2,
       next_state_1_nextstate_cell3, next_state_2_nextstate_cell0, next_state_2_nextstate_cell1,
       next_state_2_nextstate_cell2, next_state_2_nextstate_cell3, next_state_3_nextstate_cell0,
       next_state_3_nextstate_cell1, next_state_3_nextstate_cell2, next_state_3_nextstate_cell3,
       next_state_4_nextstate_cell0, next_state_4_nextstate_cell1, next_state_4_nextstate_cell2,
       next_state_4_nextstate_cell3;
  wire [7:0] multiplexer_1_out, multiplexer_2_out, multiplexer_3_out, multiplexer_4_out;

  Multiplexer #(.select(2), .width(8)) multiplexer_1 (
    .in0({in_3, in_4, in_5, in_6}), .in1({in_6, in_5, in_4, in_3}), .in2({in_15, in_11, in_7, in_3}),
    .in3({in_3, in_7, in_11, in_15}), .out(multiplexer_1_out), .sel(in_2));  // open: en
  Multiplexer #(.select(2), .width(8)) multiplexer_2 (
    .in0({in_7, in_8, in_9, in_10}), .in1({in_10, in_9, in_8, in_7}), .in2({in_16, in_12, in_8, in_4}),
    .in3({in_4, in_8, in_12, in_16}), .out(multiplexer_2_out), .sel(in_2));  // open: en
  Multiplexer #(.select(2), .width(8)) multiplexer_3 (
    .in0({in_11, in_12, in_13, in_14}), .in1({in_14, in_13, in_12, in_11}), .in2({in_17, in_13, in_9, in_5}),
    .in3({in_5, in_9, in_13, in_17}), .out(multiplexer_3_out), .sel(in_2));  // open: en
  Multiplexer #(.select(2), .width(8)) multiplexer_4 (
    .in0({in_15, in_16, in_17, in_18}), .in1({in_18, in_17, in_16, in_15}),
    .in2({in_18, in_14, in_10, in_6}), .in3({in_6, in_10, in_14, in_18}), .out(multiplexer_4_out), .sel(in_2));  // open: en
  next_state next_state_1 (
    .State_Row(multiplexer_1_out), .NextState_Cell3(next_state_1_nextstate_cell3),
    .NextState_Cell2(next_state_1_nextstate_cell2), .NextState_Cell1(next_state_1_nextstate_cell1),
    .NextState_Cell0(next_state_1_nextstate_cell0), .PlayLock(in_1), .Stable(next_state_1_stable));
  next_state next_state_2 (
    .State_Row(multiplexer_2_out), .NextState_Cell3(next_state_2_nextstate_cell3),
    .NextState_Cell2(next_state_2_nextstate_cell2), .NextState_Cell1(next_state_2_nextstate_cell1),
    .NextState_Cell0(next_state_2_nextstate_cell0), .PlayLock(in_1), .Stable(next_state_2_stable));
  next_state next_state_3 (
    .State_Row(multiplexer_3_out), .NextState_Cell3(next_state_3_nextstate_cell3),
    .NextState_Cell2(next_state_3_nextstate_cell2), .NextState_Cell1(next_state_3_nextstate_cell1),
    .NextState_Cell0(next_state_3_nextstate_cell0), .PlayLock(in_1), .Stable(next_state_3_stable));
  next_state next_state_4 (
    .State_Row(multiplexer_4_out), .NextState_Cell3(next_state_4_nextstate_cell3),
    .NextState_Cell2(next_state_4_nextstate_cell2), .NextState_Cell1(next_state_4_nextstate_cell1),
    .NextState_Cell0(next_state_4_nextstate_cell0), .PlayLock(in_1), .Stable(next_state_4_stable));
  nand nand_1 (out_35, next_state_1_stable, next_state_2_stable, next_state_3_stable, next_state_4_stable);
  Multiplexer #(.select(2), .width(2)) multiplexer_5 (
    .in0(next_state_1_nextstate_cell3), .in1(next_state_1_nextstate_cell0),
    .in2(next_state_1_nextstate_cell0), .in3(next_state_1_nextstate_cell3), .out(y00), .sel(in_2));  // open: en
  Multiplexer #(.select(2), .width(2)) multiplexer_6 (
    .in0(next_state_1_nextstate_cell2), .in1(next_state_1_nextstate_cell1),
    .in2(next_state_2_nextstate_cell0), .in3(next_state_2_nextstate_cell3), .out(y01), .sel(in_2));  // open: en
  Multiplexer #(.select(2), .width(2)) multiplexer_7 (
    .in0(next_state_1_nextstate_cell1), .in1(next_state_1_nextstate_cell2),
    .in2(next_state_3_nextstate_cell0), .in3(next_state_3_nextstate_cell3), .out(y02), .sel(in_2));  // open: en
  Multiplexer #(.select(2), .width(2)) multiplexer_8 (
    .in0(next_state_1_nextstate_cell0), .in1(next_state_1_nextstate_cell3),
    .in2(next_state_4_nextstate_cell0), .in3(next_state_4_nextstate_cell3), .out(y03), .sel(in_2));  // open: en
  Multiplexer #(.select(2), .width(2)) multiplexer_9 (
    .in0(next_state_2_nextstate_cell3), .in1(next_state_2_nextstate_cell0),
    .in2(next_state_1_nextstate_cell1), .in3(next_state_1_nextstate_cell2), .out(y04), .sel(in_2));  // open: en
  Multiplexer #(.select(2), .width(2)) multiplexer_10 (
    .in0(next_state_2_nextstate_cell2), .in1(next_state_2_nextstate_cell1),
    .in2(next_state_2_nextstate_cell1), .in3(next_state_2_nextstate_cell2), .out(y05), .sel(in_2));  // open: en
  Multiplexer #(.select(2), .width(2)) multiplexer_11 (
    .in0(next_state_2_nextstate_cell1), .in1(next_state_2_nextstate_cell2),
    .in2(next_state_3_nextstate_cell1), .in3(next_state_3_nextstate_cell2), .out(y06), .sel(in_2));  // open: en
  Multiplexer #(.select(2), .width(2)) multiplexer_12 (
    .in0(next_state_2_nextstate_cell0), .in1(next_state_2_nextstate_cell3),
    .in2(next_state_4_nextstate_cell1), .in3(next_state_4_nextstate_cell2), .out(y07), .sel(in_2));  // open: en
  Multiplexer #(.select(2), .width(2)) multiplexer_13 (
    .in0(next_state_3_nextstate_cell3), .in1(next_state_3_nextstate_cell0),
    .in2(next_state_1_nextstate_cell2), .in3(next_state_1_nextstate_cell1), .out(y08), .sel(in_2));  // open: en
  Multiplexer #(.select(2), .width(2)) multiplexer_14 (
    .in0(next_state_3_nextstate_cell2), .in1(next_state_3_nextstate_cell1),
    .in2(next_state_2_nextstate_cell2), .in3(next_state_2_nextstate_cell1), .out(y09), .sel(in_2));  // open: en
  Multiplexer #(.select(2), .width(2)) multiplexer_15 (
    .in0(next_state_3_nextstate_cell1), .in1(next_state_3_nextstate_cell2),
    .in2(next_state_3_nextstate_cell2), .in3(next_state_3_nextstate_cell1), .out(y10), .sel(in_2));  // open: en
  Multiplexer #(.select(2), .width(2)) multiplexer_16 (
    .in0(next_state_3_nextstate_cell0), .in1(next_state_3_nextstate_cell3),
    .in2(next_state_4_nextstate_cell2), .in3(next_state_4_nextstate_cell1), .out(y11), .sel(in_2));  // open: en
  Multiplexer #(.select(2), .width(2)) multiplexer_17 (
    .in0(next_state_4_nextstate_cell3), .in1(next_state_4_nextstate_cell0),
    .in2(next_state_1_nextstate_cell3), .in3(next_state_1_nextstate_cell0), .out(y12), .sel(in_2));  // open: en
  Multiplexer #(.select(2), .width(2)) multiplexer_18 (
    .in0(next_state_4_nextstate_cell2), .in1(next_state_4_nextstate_cell1),
    .in2(next_state_2_nextstate_cell3), .in3(next_state_2_nextstate_cell0), .out(y13), .sel(in_2));  // open: en
  Multiplexer #(.select(2), .width(2)) multiplexer_19 (
    .in0(next_state_4_nextstate_cell1), .in1(next_state_4_nextstate_cell2),
    .in2(next_state_3_nextstate_cell3), .in3(next_state_3_nextstate_cell0), .out(y14), .sel(in_2));  // open: en
  Multiplexer #(.select(2), .width(2)) multiplexer_20 (
    .in0(next_state_4_nextstate_cell0), .in1(next_state_4_nextstate_cell3),
    .in2(next_state_4_nextstate_cell3), .in3(next_state_4_nextstate_cell0), .out(y15), .sel(in_2));  // open: en
endmodule

module random (
  input  [3:0] in_1,
  input  in_2,
  input  in_3,
  input  in_4,
  input  in_5,
  input  in_6,
  input  in_7,
  input  in_8,
  input  in_9,
  input  in_10,
  input  in_11,
  input  in_12,
  input  in_13,
  input  in_14,
  input  in_15,
  input  in_16,
  input  in_17,
  output out_18,
  output out_19,
  output out_20,
  output out_21,
  output out_22,
  output out_23,
  output out_24,
  output out_25,
  output out_26,
  output out_27,
  output out_28,
  output out_29,
  output out_30,
  output out_31,
  output out_32,
  output out_33
);

  wire decoder_1_out0, decoder_1_out1, decoder_1_out2, decoder_1_out3, decoder_1_out4, decoder_1_out5,
       decoder_1_out6, decoder_1_out7, decoder_1_out8, decoder_1_out9, decoder_1_out10, decoder_1_out11,
       decoder_1_out12, decoder_1_out13, decoder_1_out14, decoder_1_out15, transistors_1_out_5,
       transistors_2_out_5, transistors_3_out_5, transistors_4_out_5, transistors_5_out_5,
       transistors_6_out_5, transistors_7_out_5, transistors_8_out_5, transistors_9_out_5,
       transistors_10_out_5, transistors_11_out_5, transistors_12_out_5, transistors_13_out_5,
       transistors_14_out_5, transistors_15_out_5, transistors_16_out_5;

  Decoder #(.select(4)) decoder_1 (
    .out0(decoder_1_out0), .out1(decoder_1_out1), .out2(decoder_1_out2), .out3(decoder_1_out3),
    .out4(decoder_1_out4), .out5(decoder_1_out5), .out6(decoder_1_out6), .out7(decoder_1_out7),
    .out8(decoder_1_out8), .out9(decoder_1_out9), .out10(decoder_1_out10), .out11(decoder_1_out11),
    .out12(decoder_1_out12), .out13(decoder_1_out13), .out14(decoder_1_out14), .out15(decoder_1_out15),
    .sel(in_1));  // open: en
  transistors transistors_1 (
    .random(decoder_1_out0), .stato_cella(in_2), .in_1(transistors_16_out_5), .out_5(transistors_1_out_5),
    .incremento(out_18));
  transistors transistors_2 (
    .random(decoder_1_out1), .stato_cella(in_3), .in_1(transistors_1_out_5), .out_5(transistors_2_out_5),
    .incremento(out_19));
  transistors transistors_3 (
    .random(decoder_1_out2), .stato_cella(in_4), .in_1(transistors_2_out_5), .out_5(transistors_3_out_5),
    .incremento(out_20));
  transistors transistors_4 (
    .random(decoder_1_out3), .stato_cella(in_5), .in_1(transistors_3_out_5), .out_5(transistors_4_out_5),
    .incremento(out_21));
  transistors transistors_5 (
    .random(decoder_1_out4), .stato_cella(in_6), .in_1(transistors_4_out_5), .out_5(transistors_5_out_5),
    .incremento(out_22));
  transistors transistors_6 (
    .random(decoder_1_out5), .stato_cella(in_7), .in_1(transistors_5_out_5), .out_5(transistors_6_out_5),
    .incremento(out_23));
  transistors transistors_7 (
    .random(decoder_1_out6), .stato_cella(in_8), .in_1(transistors_6_out_5), .out_5(transistors_7_out_5),
    .incremento(out_24));
  transistors transistors_8 (
    .random(decoder_1_out7), .stato_cella(in_9), .in_1(transistors_7_out_5), .out_5(transistors_8_out_5),
    .incremento(out_25));
  transistors transistors_9 (
    .random(decoder_1_out8), .stato_cella(in_10), .in_1(transistors_8_out_5), .out_5(transistors_9_out_5),
    .incremento(out_26));
  transistors transistors_10 (
    .random(decoder_1_out9), .stato_cella(in_11), .in_1(transistors_9_out_5), .out_5(transistors_10_out_5),
    .incremento(out_27));
  transistors transistors_11 (
    .random(decoder_1_out10), .stato_cella(in_12), .in_1(transistors_10_out_5), .out_5(transistors_11_out_5),
    .incremento(out_28));
  transistors transistors_12 (
    .random(decoder_1_out11), .stato_cella(in_13), .in_1(transistors_11_out_5), .out_5(transistors_12_out_5),
    .incremento(out_29));
  transistors transistors_13 (
    .random(decoder_1_out12), .stato_cella(in_14), .in_1(transistors_12_out_5), .out_5(transistors_13_out_5),
    .incremento(out_30));
  transistors transistors_14 (
    .random(decoder_1_out13), .stato_cella(in_15), .in_1(transistors_13_out_5), .out_5(transistors_14_out_5),
    .incremento(out_31));
  transistors transistors_15 (
    .random(decoder_1_out14), .stato_cella(in_16), .in_1(transistors_14_out_5), .out_5(transistors_15_out_5),
    .incremento(out_32));
  transistors transistors_16 (
    .random(decoder_1_out15), .stato_cella(in_17), .in_1(transistors_15_out_5), .out_5(transistors_16_out_5),
    .incremento(out_33));
endmodule

module transistors (
  input  in_1,
  input  random,
  input  stato_cella,
  output incremento,
  output out_5
);

  wire not_1_out, or_1_out;

  or or_1 (or_1_out, in_1, random);
  not not_1 (not_1_out, stato_cella);
  Transistor transistor_1 (.in(or_1_out), .out(out_5), .gate(not_1_out));
  Transistor transistor_2 (.in(or_1_out), .out(incremento), .gate(stato_cella));
  Pull_Resistor pull_resistor_1 (.node(incremento));
  Pull_Resistor pull_resistor_2 (.node(out_5));
endmodule
